# Fritzing sketch Wiegedings (saved by Fritzing 0.9.5d)
breadboards: 1

parts:
  LoadCell = HX711 Weighing Sensor Module
  part = ESP8266 WiFi Module [part_number=ESP8266]
  AC/DC = WX-DC12003 [package=THT]
  PGM = Pushbutton [package=THT]
  FTDI = FTDI Basic Programmer
  part_2 = Resistor [tolerance=±5% resistance=10k package=THT]
  part_3 = Resistor [tolerance=±5% resistance=10k package=THT]
  part_4 = Resistor [tolerance=±5% resistance=10k package=THT]
  part_5 = Resistor [tolerance=±5% resistance=10k package=THT]
  RST = Pushbutton [package=THT]
  U2 = V_REG_LD1117VXX [package=78xxl]
  part_6 = Electrolytic Capacitor [capacitance=470µF package="100 mil [THT, electrolytic]"]
  part_7 = Ceramic Capacitor [capacitance=10µF package="100 mil [THT, multilayer]"]
  part_8 = Ceramic Capacitor [capacitance=100µF package="100 mil [THT, multilayer]"]

nets:
  VCC: LoadCell.VCC, part.VCC, part_2.Pin_1, part_3.Pin_1, part_4.Pin_1, part_5.Pin_1, U2.OUT, part_6.+, part_8.1
  GND: LoadCell.GND, part.GND, AC/DC.DC_OUT-, PGM.leg0, FTDI.GND, RST.leg0, U2.GND, part_6.-, part_7.0, part_8.0
  N1: LoadCell.DO/RX, part.GPIO_0, PGM.leg1, part_4.Pin_0
  N2: LoadCell.CK/TX, part.GPIO_2, part_5.Pin_0
  N3: part.RXD, FTDI.TXO
  N4: part.RST, part_3.Pin_0, RST.leg1
  N5: part.CH_PD, part_2.Pin_0
  N6: part.TXD, FTDI.RXI
  N7: AC/DC.DC_OUT+, U2.IN, part_7.1

custom parts:
  ESP8266 WiFi Module: Generic WiFi Module based on the ESP8266 with onboard PCB antenna and UART communications
  WX-DC12003: Ac to DC power supply 110/220V in 5v 700ma or 12 V 300ma out.
